# Fritzing sketch TomBoy_dev (saved by Fritzing 0.9.3b)
circuit board: 8cm x 9cm
perfboards: 1

parts:
  Nokia_5110_LCD_Module1 = Nokia 5110 LCD
  U1 = JOYSTICK-PSP1000 [package=joystick-psp1000]
  S5 = Tactile Switch Buttons - 12mm Square [package=tactile-pth-12mm]
  S6 = Tactile Switch Buttons - 12mm Square [package=tactile-pth-12mm]
  S7 = Tactile Switch Buttons - 12mm Square [package=tactile-pth-12mm]
  S8 = Tactile Switch Buttons - 12mm Square [package=tactile-pth-12mm]
  R2 = Resistor [tolerance=±5% resistance=10k package=THT]
  R3 = Resistor [tolerance=±5% resistance=10k package=THT]
  R4 = Resistor [tolerance=±5% resistance=10k package=THT]
  J1 = male pin header, 4 pins [form="♂ (male)"]
  J2 = male pin header, 6 pins [form="♂ (male)"]
  J3 = male pin header, 2 pins [form="♂ (male)"]
  J4 = male pin header, 2 pins [form="♂ (male)"]
  R1 = Resistor [tolerance=±5% resistance=10k package=THT]
  R5 = Resistor [tolerance=±5% resistance=10k package=THT]
  R6 = Resistor [tolerance=±5% resistance=10k package=THT]
  R7 = Resistor [tolerance=±5% resistance=10k package=THT]
  R8 = Resistor [tolerance=±5% resistance=10k package=THT]
  R9 = Resistor [tolerance=±5% resistance=1k package=THT]
  R10 = Resistor [tolerance=±5% resistance=330 package=THT]

nets:
  VCC: Nokia_5110_LCD_Module1.VCC, U1.VCC, S5.1, S5.3, S6.1, S6.3, S7.1, S7.3, S8.1, S8.3, J4.pin2
  GND: Nokia_5110_LCD_Module1.GND, Nokia_5110_LCD_Module1.GND_(out), U1.GND, R2.Pin_1, R3.Pin_1, R4.Pin_1, J4.pin1, R1.Pin_1
  N1: Nokia_5110_LCD_Module1.SCE, Nokia_5110_LCD_Module1.SCE_(out), R9.Pin_1
  N2: Nokia_5110_LCD_Module1.RST, Nokia_5110_LCD_Module1.RST_(out), R8.Pin_1
  N3: Nokia_5110_LCD_Module1.D/C, Nokia_5110_LCD_Module1.D/C_(out), R7.Pin_1
  N4: Nokia_5110_LCD_Module1.DN(MOSI), R6.Pin_1
  N5: Nokia_5110_LCD_Module1.SCLK, R5.Pin_1
  N6: Nokia_5110_LCD_Module1.LED, R10.Pin_1
  N7: U1.X, J3.pin2
  N8: U1.Y, J3.pin1
  N9: S5.2, S5.4, R4.Pin_0, J1.pin3
  N10: S6.2, S6.4, J1.pin2, R1.Pin_0
  N11: S7.2, S7.4, R2.Pin_0, J1.pin1
  N12: S8.2, S8.4, R3.Pin_0, J1.pin4
  N13: J2.pin1, R9.Pin_0
  N14: J2.pin2, R8.Pin_0
  N15: J2.pin3, R7.Pin_0
  N16: J2.pin4, R6.Pin_0
  N17: J2.pin5, R5.Pin_0
  N18: J2.pin6, R10.Pin_0

custom parts:
  Nokia 5110 LCD: Nokia 5110 Graphic 84*48 LCD module such as the Sparkfun LCD-10168 or the clones from Ebay. There is example code for the Arduino available from the Sparkfun site in https://learn.sparkfun.com/tutorials/graphic-lcd-hookup-guide This is a 3.3V device, if you are running it from a 5V micro you need a 5V tolorant level translator such as the 74ahc367 to protect the signal imputs. Rafa G. did a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
  Tactile Switch Buttons - 12mm Square: Medium-sized clicky momentary switches are standard input "buttons" on electronic projects. These work best in a PCB but can be used on a solderless breadboard as shown in this tutorial. The pins are normally open (disconnected) and when the button is pressed they are momentarily closed. They come in a pack of 10, they're pretty handy so you'll want to keep them around. You can find an EAGLE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
